# Fritzing sketch DaisyDrone (saved by Fritzing 0.9.4)
breadboards: 1

parts:
  SOM1 = Daisy Seed [chip_label=IC package="DIP (Dual Inline) [THT]"]
  R1 = Rotary Potentiometer (Small) [maximum_resistance=100kΩ package=THT]
  R2 = Rotary Potentiometer (Small) [maximum_resistance=100kΩ package=THT]
  R3 = Rotary Potentiometer (Small) [maximum_resistance=100kΩ package=THT]
  U1 = 3.5mm Audio Jack [package=audio-jack-3.5mm-smd]
  S1 = Pushbutton [package="[THT]"]

nets:
  N1: SOM1.pin_18, U1.RIGHT
  N2: SOM1.pin_20, SOM1.pin_40, R1.leg1, R2.leg1, R3.leg1, U1.SLEEVE
  N3: SOM1.pin_21, R1.leg2, R2.leg2, R3.leg2, S1.Pin_1, S1.Pin_2
  N4: SOM1.pin_26, R3.wiper
  N5: SOM1.pin_27, R2.wiper
  N6: SOM1.pin_28, R1.wiper
  N7: SOM1.pin_35, S1.Pin_3, S1.Pin_4

notes:
  OSC1
  OSC2
  LFO
  WAVEFORM

custom parts:
  Daisy Seed: Daisy is an embedded platform for music. It features everything you need for creating high fidelity audio hardware devices. Just plug in a USB cable and start making sound! No soldering required.
